// Logisim project Logisim_Jokenpo.circ as structural Verilog: 4 circuits, main circuit main
module main (
  input  in_1,
  input  in_2,
  input  in_3,
  input  in_4,
  input  in_5,
  input  in_6
);

  wire codificador_1_out_4, codificador_1_out_5, codificador_2_out_4, codificador_2_out_5,
       decodificador_1_empate, decodificador_1_invalido, decodificador_1_vitoriaj1,
       decodificador_1_vitoriaj2, solucionador_1_jogador1, solucionador_1_jogador2;

  Codificador codificador_1 (
    .Papel(in_1), .Pedra(in_2), .Tesoura(in_3), .out_4(codificador_1_out_4), .out_5(codificador_1_out_5));
  Codificador codificador_2 (
    .Papel(in_4), .Pedra(in_5), .Tesoura(in_6), .out_4(codificador_2_out_4), .out_5(codificador_2_out_5));
  Solucionador solucionador_1 (
    .A(codificador_1_out_4), .B(codificador_1_out_5), .C(codificador_2_out_4), .D(codificador_2_out_5),
    .JOGADOR1(solucionador_1_jogador1), .JOGADOR2(solucionador_1_jogador2));
  LED led_1 (.in(decodificador_1_invalido));
  Decodificador decodificador_1 (
    .A(solucionador_1_jogador1), .B(solucionador_1_jogador2), .INVALIDO(decodificador_1_invalido),
    .VITORIAJ1(decodificador_1_vitoriaj1), .VITORIAJ2(decodificador_1_vitoriaj2),
    .EMPATE(decodificador_1_empate));
  LED led_2 (.in(decodificador_1_vitoriaj1));
  LED led_3 (.in(decodificador_1_vitoriaj2));
  LED led_4 (.in(decodificador_1_empate));

  // Notes on the sheet:
  //   Jogador 1
  //   Jogador 2
endmodule

module Solucionador (
  input  A,
  input  B,
  input  C,
  input  D,
  output JOGADOR1,
  output JOGADOR2
);

  wire not_1_out, not_2_out, not_3_out, not_4_out, X1_out, X2_out, Y1_out, Y2_out, Y3_out, Z1_out, Z2_out,
       Z3_out;

  not not_1 (not_1_out, A);
  not not_2 (not_2_out, B);
  not not_3 (not_3_out, C);
  not not_4 (not_4_out, D);
  and Y1 (Y1_out, not_1_out, B, D);
  and X1 (X1_out, A, not_2_out, not_3_out, D);
  and Y2 (Y2_out, A, C, not_4_out);
  and Y3 (Y3_out, B, C, D);
  and Z1 (Z1_out, B, not_3_out, D);
  and X2 (X2_out, not_1_out, B, C, not_4_out);
  and Z2 (Z2_out, A, not_2_out, C);
  and Z3 (Z3_out, A, C, D);
  or or_1 (JOGADOR1, Y1_out, X1_out, Y2_out, Y3_out);
  or or_2 (JOGADOR2, Z1_out, X2_out, Z2_out, Z3_out);
endmodule

module Codificador (
  input  Papel,
  input  Pedra,
  input  Tesoura,
  output out_4,
  output out_5
);

  wire and_1_out, and_2_out, and_3_out, and_4_out;

  and and_1 (and_1_out, Papel, ~Pedra, ~Tesoura);  // AND_Gate
  and and_2 (and_2_out, ~Papel, ~Pedra, Tesoura);  // AND_Gate
  and and_3 (and_3_out, ~Papel, ~Pedra, Tesoura);  // AND_Gate
  and and_4 (and_4_out, ~Papel, Pedra, ~Tesoura);  // AND_Gate
  or or_1 (out_4, and_1_out, and_2_out);
  or or_2 (out_5, and_3_out, and_4_out);
endmodule

module Decodificador (
  input  A,
  input  B,
  output INVALIDO,
  output VITORIAJ1,
  output VITORIAJ2,
  output EMPATE
);

  wire not_1_out, not_2_out;

  not not_1 (not_1_out, A);
  not not_2 (not_2_out, B);
  and and_1 (INVALIDO, not_1_out, not_2_out);
  and and_2 (VITORIAJ1, A, not_2_out);
  and and_3 (VITORIAJ2, not_1_out, B);
  and and_4 (EMPATE, A, B);
endmodule
